// Logisim project template_alu.circ as structural Verilog: 6 circuits, main circuit alu
module alu (
  input  a,
  input  b,
  input  [1:0] opcode,
  input  CLK,
  output [7:0] c
);

  wire opcode_decoder_1_add_sub, opcode_decoder_1_left, opcode_decoder_1_sub;
  wire [7:0] A_t, B_t, SHIFTED, SUM;

  sipo_8 sipo_8_1 (.x(a), .CLK(CLK), .y(A_t));
  sipo_8 sipo_8_2 (.x(b), .CLK(CLK), .y(B_t));
  opcode_decoder opcode_decoder_1 (
    .opcode(opcode), .add_sub(opcode_decoder_1_add_sub), .sub(opcode_decoder_1_sub),
    .left(opcode_decoder_1_left));  // open: shift
  Multiplexer #(.width(8), .enable("false")) multiplexer_1 (
    .in0(SHIFTED), .in1(SUM), .out(c), .sel(opcode_decoder_1_add_sub));
  add_sub add_sub_1 (.a(A_t), .b(B_t), .sub(opcode_decoder_1_sub), .c(SUM));
  shifter shifter_1 (.x(A_t), .left(opcode_decoder_1_left), .y(SHIFTED));
  // Probe on c
endmodule

module sipo_8 (
  input  x,
  input  CLK,
  output [7:0] y
);

  D_Flip_Flop d_ff_1 (.clk(CLK), .D(x), .Q(y[0]));  // open: Qn, preset, en, reset
  D_Flip_Flop d_ff_2 (.clk(CLK), .D(y[0]), .Q(y[1]));  // open: Qn, preset, en, reset
  D_Flip_Flop d_ff_3 (.clk(CLK), .D(y[1]), .Q(y[2]));  // open: Qn, preset, en, reset
  D_Flip_Flop d_ff_4 (.clk(CLK), .D(y[2]), .Q(y[3]));  // open: Qn, preset, en, reset
  D_Flip_Flop d_ff_5 (.clk(CLK), .D(y[3]), .Q(y[4]));  // open: Qn, preset, en, reset
  D_Flip_Flop d_ff_6 (.clk(CLK), .D(y[4]), .Q(y[5]));  // open: Qn, preset, en, reset
  D_Flip_Flop d_ff_7 (.clk(CLK), .D(y[5]), .Q(y[6]));  // open: Qn, preset, en, reset
  D_Flip_Flop d_ff_8 (.clk(CLK), .D(y[6]), .Q(y[7]));  // open: Qn, preset, en, reset

  // Other names for the same wires on the sheet: _0 = y[0]; _1 = y[1]; _2 = y[2]; _3 = y[3]; _4 = y[4]; _5 = y[5];
  //   _6 = y[6]; _7 = y[7]
endmodule

module opcode_decoder (
  input  [1:0] opcode,
  output add_sub,
  output sub,
  output shift,
  output left
);

  wire and_1_out, not_1_out, or_1_out, xor_1_out;

  or or_1 (or_1_out, opcode[0], opcode[1]);
  and and_1 (and_1_out, opcode[0], opcode[1]);
  not not_1 (not_1_out, or_1_out);
  xor xor_1 (xor_1_out, opcode[0], opcode[1]);
  and and_2 (sub, xor_1_out, opcode[0]);
  or or_2 (add_sub, sub, not_1_out);
  and and_3 (left, xor_1_out, opcode[1]);
  or or_3 (shift, and_1_out, left);
endmodule

module add_sub (
  input  [7:0] a,
  input  [7:0] b,
  input  sub,
  output [7:0] c
);

  wire b0, b1, b2, b3, b4, b5, b6, b7, f_adder_1_carry, f_adder_2_carry, f_adder_3_carry, f_adder_4_carry,
       f_adder_5_carry, f_adder_6_carry, f_adder_7_carry;

  // Probe on a
  // Probe on b
  xor xor_1 (b0, sub, b[0]);
  xor xor_2 (b6, b[6], sub);
  xor xor_3 (b7, b[7], sub);
  F_ADDER f_adder_1 (.A(a[0]), .B(b0), .c(sub), .Sum(c[0]), .carry(f_adder_1_carry));
  xor xor_4 (b1, b[1], sub);
  xor xor_5 (b4, b[4], sub);
  xor xor_6 (b5, b[5], sub);
  F_ADDER f_adder_2 (.A(a[1]), .B(b1), .c(f_adder_1_carry), .Sum(c[1]), .carry(f_adder_2_carry));
  xor xor_7 (b2, sub, b[2]);
  F_ADDER f_adder_3 (.A(a[2]), .B(b2), .c(f_adder_2_carry), .Sum(c[2]), .carry(f_adder_3_carry));
  xor xor_8 (b3, b[3], sub);
  // Probe on c
  F_ADDER f_adder_4 (.A(a[3]), .B(b3), .c(f_adder_3_carry), .Sum(c[3]), .carry(f_adder_4_carry));
  F_ADDER f_adder_5 (.A(a[4]), .B(b4), .c(f_adder_4_carry), .Sum(c[4]), .carry(f_adder_5_carry));
  F_ADDER f_adder_6 (.A(a[5]), .B(b5), .c(f_adder_5_carry), .Sum(c[5]), .carry(f_adder_6_carry));
  F_ADDER f_adder_7 (.A(b6), .B(a[6]), .c(f_adder_6_carry), .Sum(c[6]), .carry(f_adder_7_carry));
  F_ADDER f_adder_8 (.A(b7), .B(a[7]), .c(f_adder_7_carry), .Sum(c[7]));  // open: carry
endmodule

module shifter (
  input  [7:0] x,
  input  left,
  output [7:0] y
);

  // Probe on x
  // Probe on y
  Multiplexer #(.width(8), .enable("false")) multiplexer_1 (
    .in0({{2{x[7]}}, x[6:1]}), .in1({x[6:0], 1'b0}), .out(y), .sel(left));

  // Other names for the same wires on the sheet: _0 = x[0]; _1 = x[1]; _2 = x[2]; _3 = x[3]; _4 = x[4]; _5 = x[5];
  //   _6 = x[6]; _7 = x[7]
endmodule

// FA
module F_ADDER (
  input  A,
  input  B,
  input  c,
  output Sum,
  output carry
);

  wire and_1_out, and_2_out, and_3_out, or_1_out, xor_1_out;

  xor xor_1 (xor_1_out, A, B);
  xor xor_2 (Sum, xor_1_out, c);
  and and_1 (and_1_out, A, B);
  and and_2 (and_2_out, B, c);
  and and_3 (and_3_out, A, c);
  or or_1 (or_1_out, and_1_out, and_2_out);
  or or_2 (carry, or_1_out, and_3_out);
endmodule
